// Logisim project watchdog_project.circ as structural Verilog: 1 circuit, main circuit main
module main (
  input  in_1
);

  wire clock_1_out, comparator_1_gt;
  wire [7:0] counter_1_q;

  Clock clock_1 (.out(clock_1_out));
  Counter counter_1 (.clr(in_1), .clk(clock_1_out), .Q(counter_1_q));  // open: load, up, count, D, carry
  Comparator comparator_1 (.a(counter_1_q), .b(8'h3), .gt(comparator_1_gt));  // open: eq, lt
  LED led_1 (.in(comparator_1_gt));
endmodule
